# Fritzing sketch schematic-alpha (saved by Fritzing 0.9.4)
breadboards: 1

parts:
  Raspberry_Pi1 = Raspberry Pi 2
  R1 = Resistor [tolerance=±5% resistance=220 package=THT]
  R2 = Resistor [tolerance=±5% resistance=220 package=THT]
  LED1 = LED - 5mm [color="Red (633nm)" package="5 mm [THT]"]
  LED2 = LED - 5mm [color="Green (555nm)" package="5 mm [THT]"]  # not connected

nets:
  N1: Raspberry_Pi1.GPIO17, R2.Pin_0
  N2: Raspberry_Pi1.GPIO18, R1.Pin_0
  N3: Raspberry_Pi1.GND, LED1.cathode
  N4: R1.Pin_1, LED1.anode
